// Logisim project CRC.circ as structural Verilog: 2 circuits, main circuit CRC
module CRC (
  input  [7:0] A,
  input  [3:0] B,
  output [10:0] C
);

  wire [2:0] n4bit_2_c, n4bit_3_c, n4bit_4_c, n4bit_5_c, n4bit_6_c, n4bit_7_c;
  wire [3:1] n4bit_1_c;

  _4bit u_4bit_1 (.A(A[7:4]), .B(B), .C(n4bit_1_c));  // open: D
  _4bit u_4bit_2 (.A({n4bit_1_c, A[3]}), .B(B), .C(n4bit_2_c));  // open: D
  _4bit u_4bit_3 (.A({n4bit_2_c, A[2]}), .B(B), .C(n4bit_3_c));  // open: D
  _4bit u_4bit_4 (.A({n4bit_3_c, A[1]}), .B(B), .C(n4bit_4_c));  // open: D
  _4bit u_4bit_5 (.A({n4bit_4_c, A[0]}), .B(B), .C(n4bit_5_c));  // open: D
  _4bit u_4bit_6 (.A({n4bit_5_c, 1'b0}), .B(B), .C(n4bit_6_c));  // open: D
  _4bit u_4bit_7 (.A({n4bit_6_c, 1'b0}), .B(B), .C(n4bit_7_c));  // open: D
  _4bit u_4bit_8 (.A({n4bit_7_c, 1'b0}), .B(B), .C(C[2:0]));  // open: D

  assign C[10:3] = A;

  // Other names for the same wires on the sheet: ans[2:0] = C[2:0]
endmodule

module _4bit (
  input  [3:0] A,
  input  [3:0] B,
  output [2:0] C,
  output D
);

  wire [2:0] ans;

  xor xor_1 (ans[0], A[0], B[0]);
  xor xor_2 (ans[1], A[1], B[1]);
  xor xor_3 (ans[2], A[2], B[2]);
  Multiplexer #(.width(3)) multiplexer_1 (.in0(A[2:0]), .in1(ans), .out(C), .sel(A[3]));  // open: en
  Multiplexer multiplexer_2 (.in0(1'b0), .in1(1'b1), .out(D), .sel(A[3]));  // open: en
endmodule
