// Logisim project fsm.circ as structural Verilog: 2 circuits, main circuit fsm
module fsm (
  input  clr,
  input  [1:0] in,
  output z
);

  wire clk, clr_t, register_1_q;
  wire [2:0] next_1_b0, register_2_q;

  Register #(.width(1)) register_1 (.D(clr), .Q(register_1_q), .clk(clk));  // open: en, clr
  Clock clock_1 (.out(clk));
  Multiplexer multiplexer_1 (.in0(1'b0), .in1(register_1_q), .out(clr_t), .sel(clr));  // open: en
  Register #(.width(3)) register_2 (.D(next_1_b0), .Q(register_2_q), .clk(clk), .clr(clr_t));  // open: en
  next next_1 (
    .a2(register_2_q[2]), .a1(register_2_q[1]), .a0(register_2_q[0]), .s1(in[1]), .s0(in[0]),
    .b2(next_1_b0[2]), .b1(next_1_b0[1]), .b0(next_1_b0[0]), .z(z));
endmodule

module next (
  input  a2,
  input  a1,
  input  a0,
  input  s1,
  input  s0,
  output b2,
  output b1,
  output b0,
  output z
);

  wire and_1_out, and_2_out, and_3_out, and_4_out, and_5_out, and_6_out, and_7_out, and_8_out, and_9_out,
       and_10_out, and_11_out, and_12_out, not_1_out, not_2_out, not_3_out, not_4_out, not_5_out, not_6_out,
       not_7_out, not_8_out, not_9_out, not_10_out, not_11_out, not_12_out, not_13_out, not_14_out,
       not_15_out, not_16_out, not_17_out, not_18_out, not_19_out, not_20_out, not_21_out, not_22_out,
       not_23_out, not_24_out, not_25_out, not_26_out, not_27_out, not_28_out, not_29_out, not_30_out;

  not not_1 (not_1_out, a2);
  not not_2 (not_2_out, a1);
  not not_3 (not_3_out, s0);
  not not_4 (not_4_out, a2);
  not not_5 (not_5_out, a0);
  not not_6 (not_6_out, s0);
  not not_7 (not_7_out, a2);
  not not_8 (not_8_out, a1);
  not not_9 (not_9_out, s1);
  not not_10 (not_10_out, a2);
  not not_11 (not_11_out, a0);
  not not_12 (not_12_out, s1);
  not not_13 (not_13_out, a2);
  not not_14 (not_14_out, a0);
  not not_15 (not_15_out, s0);
  not not_16 (not_16_out, a1);
  not not_17 (not_17_out, a0);
  not not_18 (not_18_out, s1);
  not not_19 (not_19_out, a2);
  not not_20 (not_20_out, a1);
  not not_21 (not_21_out, s1);
  not not_22 (not_22_out, s0);
  not not_23 (not_23_out, a2);
  not not_24 (not_24_out, a0);
  not not_25 (not_25_out, s1);
  not not_26 (not_26_out, s0);
  not not_27 (not_27_out, s1);
  not not_28 (not_28_out, s1);
  not not_29 (not_29_out, s0);
  not not_30 (not_30_out, s0);
  and and_1 (and_1_out, not_1_out, not_2_out, a0, s1, not_3_out);
  and and_2 (and_2_out, not_4_out, a1, not_5_out, not_6_out);
  and and_3 (and_3_out, not_7_out, not_8_out, a0, not_9_out);
  and and_4 (and_4_out, not_10_out, a1, not_11_out, not_12_out, s0);
  and and_5 (and_5_out, not_13_out, a1, not_14_out, s1, not_15_out);
  and and_6 (and_6_out, not_16_out, not_17_out, not_18_out, s0);
  and and_7 (and_7_out, not_19_out, not_20_out, a0, not_21_out, not_22_out);
  and and_8 (and_8_out, not_23_out, a1, not_24_out, not_25_out, not_26_out);
  and and_9 (and_9_out, a1, a0, not_27_out, s0);
  and and_10 (and_10_out, a2, not_28_out, s0);
  and and_11 (and_11_out, a1, a0, not_29_out);
  and and_12 (and_12_out, a2, not_30_out);
  or or_1 (b2, and_1_out, and_2_out);
  or or_2 (b1, and_3_out, and_4_out, and_5_out);
  or or_3 (b0, and_6_out, and_7_out, and_8_out, and_9_out, and_10_out);
  or or_4 (z, and_11_out, and_12_out);
endmodule
