// Logisim project grf.circ as structural Verilog: 2 circuits, main circuit grf
module grf (
  input  clk,
  input  reset,
  input  WE,
  input  [4:0] A1,
  input  [4:0] A2,
  input  [4:0] A3,
  input  [31:0] WD,
  output [31:0] RD1,
  output [31:0] RD2
);

  wire [31:0] demultiplexer_1_out0, demultiplexer_1_out1, demultiplexer_1_out2, demultiplexer_1_out3,
       demultiplexer_1_out4, demultiplexer_1_out5, demultiplexer_1_out6, demultiplexer_1_out7,
       demultiplexer_1_out8, demultiplexer_1_out9, demultiplexer_1_out10, demultiplexer_1_out11,
       demultiplexer_1_out12, demultiplexer_1_out13, demultiplexer_1_out14, demultiplexer_1_out15,
       demultiplexer_1_out16, demultiplexer_1_out17, demultiplexer_1_out18, demultiplexer_1_out19,
       demultiplexer_1_out20, demultiplexer_1_out21, demultiplexer_1_out22, demultiplexer_1_out23,
       demultiplexer_1_out24, demultiplexer_1_out25, demultiplexer_1_out26, demultiplexer_1_out27,
       demultiplexer_1_out28, demultiplexer_1_out29, demultiplexer_1_out30, demultiplexer_1_out31, out0,
       out1, out2, out3, out4, out5, out6, out7, out8, out9, out10, out11, out12, out13, out14, out15, out16,
       out17, out18, out19, out20, out21, out22, out23, out24, out25, out26, out27, out28, out29, out30,
       out31;

  Demultiplexer #(.select(5), .width(32), .tristate("true")) demultiplexer_1 (
    .out0(demultiplexer_1_out0), .out1(demultiplexer_1_out1), .out2(demultiplexer_1_out2),
    .out3(demultiplexer_1_out3), .out4(demultiplexer_1_out4), .out5(demultiplexer_1_out5),
    .out6(demultiplexer_1_out6), .out7(demultiplexer_1_out7), .out8(demultiplexer_1_out8),
    .out9(demultiplexer_1_out9), .out10(demultiplexer_1_out10), .out11(demultiplexer_1_out11),
    .out12(demultiplexer_1_out12), .out13(demultiplexer_1_out13), .out14(demultiplexer_1_out14),
    .out15(demultiplexer_1_out15), .out16(demultiplexer_1_out16), .out17(demultiplexer_1_out17),
    .out18(demultiplexer_1_out18), .out19(demultiplexer_1_out19), .out20(demultiplexer_1_out20),
    .out21(demultiplexer_1_out21), .out22(demultiplexer_1_out22), .out23(demultiplexer_1_out23),
    .out24(demultiplexer_1_out24), .out25(demultiplexer_1_out25), .out26(demultiplexer_1_out26),
    .out27(demultiplexer_1_out27), .out28(demultiplexer_1_out28), .out29(demultiplexer_1_out29),
    .out30(demultiplexer_1_out30), .out31(demultiplexer_1_out31), .in(WD), .sel(A3));  // open: en
  \reg  reg_1 (
    .in0(demultiplexer_1_out0), .in1(demultiplexer_1_out1), .in2(demultiplexer_1_out2),
    .in3(demultiplexer_1_out3), .in4(demultiplexer_1_out4), .in5(demultiplexer_1_out5),
    .in6(demultiplexer_1_out6), .in7(demultiplexer_1_out7), .in8(demultiplexer_1_out8),
    .in9(demultiplexer_1_out9), .in10(demultiplexer_1_out10), .in11(demultiplexer_1_out11),
    .in12(demultiplexer_1_out12), .in13(demultiplexer_1_out13), .in14(demultiplexer_1_out14),
    .in15(demultiplexer_1_out15), .in16(demultiplexer_1_out16), .in17(demultiplexer_1_out17),
    .in18(demultiplexer_1_out18), .in19(demultiplexer_1_out19), .in20(demultiplexer_1_out20),
    .in21(demultiplexer_1_out21), .in22(demultiplexer_1_out22), .in23(demultiplexer_1_out23),
    .in24(demultiplexer_1_out24), .in25(demultiplexer_1_out25), .in26(demultiplexer_1_out26),
    .in27(demultiplexer_1_out27), .in28(demultiplexer_1_out28), .in29(demultiplexer_1_out29),
    .in30(demultiplexer_1_out30), .in31(demultiplexer_1_out31), .clk(clk), .reset(reset), .en(WE),
    .out0(out0), .out1(out1), .out2(out2), .out3(out3), .out4(out4), .out5(out5), .out6(out6), .out7(out7),
    .out8(out8), .out9(out9), .out10(out10), .out11(out11), .out12(out12), .out13(out13), .out14(out14),
    .out15(out15), .out16(out16), .out17(out17), .out18(out18), .out19(out19), .out20(out20), .out21(out21),
    .out22(out22), .out23(out23), .out24(out24), .out25(out25), .out26(out26), .out27(out27), .out28(out28),
    .out29(out29), .out30(out30), .out31(out31));
  Multiplexer #(.select(5), .width(32)) multiplexer_1 (
    .in0(out0), .in1(out1), .in2(out2), .in3(out3), .in4(out4), .in5(out5), .in6(out6), .in7(out7),
    .in8(out8), .in9(out9), .in10(out10), .in11(out11), .in12(out12), .in13(out13), .in14(out14),
    .in15(out15), .in16(out16), .in17(out17), .in18(out18), .in19(out19), .in20(out20), .in21(out21),
    .in22(out22), .in23(out23), .in24(out24), .in25(out25), .in26(out26), .in27(out27), .in28(out28),
    .in29(out29), .in30(out30), .in31(out31), .out(RD1), .sel(A1));  // open: en
  Multiplexer #(.select(5), .width(32)) multiplexer_2 (
    .in0(out0), .in1(out1), .in2(out2), .in3(out3), .in4(out4), .in5(out5), .in6(out6), .in7(out7),
    .in8(out8), .in9(out9), .in10(out10), .in11(out11), .in12(out12), .in13(out13), .in14(out14),
    .in15(out15), .in16(out16), .in17(out17), .in18(out18), .in19(out19), .in20(out20), .in21(out21),
    .in22(out22), .in23(out23), .in24(out24), .in25(out25), .in26(out26), .in27(out27), .in28(out28),
    .in29(out29), .in30(out30), .in31(out31), .out(RD2), .sel(A2));  // open: en
endmodule

module \reg  (
  input  [31:0] in0,
  input  clk,
  input  reset,
  input  en,
  input  [31:0] in1,
  input  [31:0] in2,
  input  [31:0] in3,
  input  [31:0] in4,
  input  [31:0] in5,
  input  [31:0] in6,
  input  [31:0] in7,
  input  [31:0] in8,
  input  [31:0] in9,
  input  [31:0] in10,
  input  [31:0] in11,
  input  [31:0] in12,
  input  [31:0] in13,
  input  [31:0] in14,
  input  [31:0] in15,
  input  [31:0] in16,
  input  [31:0] in17,
  input  [31:0] in18,
  input  [31:0] in19,
  input  [31:0] in20,
  input  [31:0] in21,
  input  [31:0] in22,
  input  [31:0] in23,
  input  [31:0] in24,
  input  [31:0] in25,
  input  [31:0] in26,
  input  [31:0] in27,
  input  [31:0] in28,
  input  [31:0] in29,
  input  [31:0] in30,
  input  [31:0] in31,
  output [31:0] out0,
  output [31:0] out1,
  output [31:0] out2,
  output [31:0] out3,
  output [31:0] out4,
  output [31:0] out5,
  output [31:0] out6,
  output [31:0] out7,
  output [31:0] out8,
  output [31:0] out9,
  output [31:0] out10,
  output [31:0] out11,
  output [31:0] out12,
  output [31:0] out13,
  output [31:0] out14,
  output [31:0] out15,
  output [31:0] out16,
  output [31:0] out17,
  output [31:0] out18,
  output [31:0] out19,
  output [31:0] out20,
  output [31:0] out21,
  output [31:0] out22,
  output [31:0] out23,
  output [31:0] out24,
  output [31:0] out25,
  output [31:0] out26,
  output [31:0] out27,
  output [31:0] out28,
  output [31:0] out29,
  output [31:0] out30,
  output [31:0] out31
);

  Register #(.width(32)) _00 (.D(in0), .en(1'b0), .Q(out0), .clk(clk), .clr(reset));
  Register #(.width(32)) _08 (.D(in8), .en(en), .Q(out8), .clk(clk), .clr(reset));
  Register #(.width(32)) _16 (.D(in16), .en(en), .Q(out16), .clk(clk), .clr(reset));
  Register #(.width(32)) _24 (.D(in24), .en(en), .Q(out24), .clk(clk), .clr(reset));
  Register #(.width(32)) _01 (.D(in1), .en(en), .Q(out1), .clk(clk), .clr(reset));
  Register #(.width(32)) _09 (.D(in9), .en(en), .Q(out9), .clk(clk), .clr(reset));
  Register #(.width(32)) _17 (.D(in17), .en(en), .Q(out17), .clk(clk), .clr(reset));
  Register #(.width(32)) _25 (.D(in25), .en(en), .Q(out25), .clk(clk), .clr(reset));
  Register #(.width(32)) _02 (.D(in2), .en(en), .Q(out2), .clk(clk), .clr(reset));
  Register #(.width(32)) _10 (.D(in10), .en(en), .Q(out10), .clk(clk), .clr(reset));
  Register #(.width(32)) _18 (.D(in18), .en(en), .Q(out18), .clk(clk), .clr(reset));
  Register #(.width(32)) _26 (.D(in26), .en(en), .Q(out26), .clk(clk), .clr(reset));
  Register #(.width(32)) _03 (.D(in3), .en(en), .Q(out3), .clk(clk), .clr(reset));
  Register #(.width(32)) _11 (.D(in11), .en(en), .Q(out11), .clk(clk), .clr(reset));
  Register #(.width(32)) _19 (.D(in19), .en(en), .Q(out19), .clk(clk), .clr(reset));
  Register #(.width(32)) _27 (.D(in27), .en(en), .Q(out27), .clk(clk), .clr(reset));
  Register #(.width(32)) _04 (.D(in4), .en(en), .Q(out4), .clk(clk), .clr(reset));
  Register #(.width(32)) _12 (.D(in12), .en(en), .Q(out12), .clk(clk), .clr(reset));
  Register #(.width(32)) _20 (.D(in20), .en(en), .Q(out20), .clk(clk), .clr(reset));
  Register #(.width(32)) _28 (.D(in28), .en(en), .Q(out28), .clk(clk), .clr(reset));
  Register #(.width(32)) _05 (.D(in5), .en(en), .Q(out5), .clk(clk), .clr(reset));
  Register #(.width(32)) _13 (.D(in13), .en(en), .Q(out13), .clk(clk), .clr(reset));
  Register #(.width(32)) _21 (.D(in21), .en(en), .Q(out21), .clk(clk), .clr(reset));
  Register #(.width(32)) _29 (.D(in29), .en(en), .Q(out29), .clk(clk), .clr(reset));
  Register #(.width(32)) _06 (.D(in6), .en(en), .Q(out6), .clk(clk), .clr(reset));
  Register #(.width(32)) _14 (.D(in14), .en(en), .Q(out14), .clk(clk), .clr(reset));
  Register #(.width(32)) _22 (.D(in22), .en(en), .Q(out22), .clk(clk), .clr(reset));
  Register #(.width(32)) _30 (.D(in30), .en(en), .Q(out30), .clk(clk), .clr(reset));
  Register #(.width(32)) _07 (.D(in7), .en(en), .Q(out7), .clk(clk), .clr(reset));
  Register #(.width(32)) _15 (.D(in15), .en(en), .Q(out15), .clk(clk), .clr(reset));
  Register #(.width(32)) _23 (.D(in23), .en(en), .Q(out23), .clk(clk), .clr(reset));
  Register #(.width(32)) _31 (.D(in31), .en(en), .Q(out31), .clk(clk), .clr(reset));

  // Other names for the same wires on the sheet: res = reset
endmodule
