// Logisim project SCCPU.circ as structural Verilog: 8 circuits, main circuit main
module main (
  input  Reset,
  output [31:0] Instr,
  output RegWrite,
  output [4:0] RegAddr,
  output [31:0] RegData,
  output MemWrite,
  output [4:0] MemAddr,
  output [31:0] MemData
);

  wire Br, BSel, CLK, WDSel, WRSel, Zero;
  wire [1:0] EXTOp;
  wire [2:0] ALUOp;
  wire [31:0] alu_1_aluresult, dm_1_rd, ext_1_extout, grf_1_rd1, multiplexer_3_out;

  Clock clock_1 (.out(CLK));
  IFU ifu_1 (.imm(Instr[15:0]), .CLK(CLK), .PCReset(Reset), .Br(Br), .Zero(Zero), .RD(Instr));
  CTRL ctrl_1 (
    .funct(Instr[5:0]), .opcode(Instr[31:26]), .Br(Br), .WRSel(WRSel), .WDSel(WDSel), .EXTOp(EXTOp),
    .RFWE(RegWrite), .BSel(BSel), .ALUOp(ALUOp), .DMWR(MemWrite));
  Multiplexer #(.width(5)) multiplexer_1 (
    .in0(Instr[20:16]), .in1(Instr[15:11]), .out(RegAddr), .sel(WRSel));  // open: en
  Multiplexer #(.width(32)) multiplexer_2 (
    .in0({alu_1_aluresult[31:7], MemAddr, alu_1_aluresult[1:0]}), .in1(dm_1_rd), .out(RegData), .sel(WDSel));  // open: en
  GRF grf_1 (
    .A1(Instr[25:21]), .A2(Instr[20:16]), .A3(RegAddr), .WD(RegData), .CLK(CLK), .RFReset(Reset),
    .WE(RegWrite), .RD1(grf_1_rd1), .RD2(MemData));
  EXT ext_1 (.imm(Instr[15:0]), .EXTOp(EXTOp), .EXTOut(ext_1_extout));
  Multiplexer #(.width(32)) multiplexer_3 (
    .in0(MemData), .in1(ext_1_extout), .out(multiplexer_3_out), .sel(BSel));  // open: en
  ALU alu_1 (
    .SA(grf_1_rd1), .SB(multiplexer_3_out), .ALUOp(ALUOp), .out_4(Zero),
    .ALUResult({alu_1_aluresult[31:7], MemAddr, alu_1_aluresult[1:0]}));
  DM dm_1 (
    .A({alu_1_aluresult[31:7], MemAddr, alu_1_aluresult[1:0]}), .WD(MemData), .CLK(CLK), .Wr(MemWrite),
    .DMReset(Reset), .RD(dm_1_rd));

  // Other names for the same wires on the sheet: DMWr = MemWrite; funct[5:0] = Instr[5:0]; opcode[5:0] = Instr[31:26];
  //   RFWE = RegWrite

  // Notes on the sheet:
  //   opcode
  //   rs
  //   rt
  //   rd
  //   shamt
  //   funct
  //   imm16
endmodule

module IFU (
  input  CLK,
  input  PCReset,
  input  Br,
  input  Zero,
  input  [15:0] imm,
  output [31:0] RD
);

  wire and_1_out;
  wire [31:0] adder_1_out, adder_2_out, bit_extender_1_out, multiplexer_1_out, PC_q;

  Register #(.width(32)) PC (.D(multiplexer_1_out), .Q(PC_q), .clk(CLK), .clr(PCReset));  // open: en
  assign bit_extender_1_out = {{14{imm[15]}}, {imm, 2'b00}};  // Bit_Extender bit_extender_1
  Adder #(.width(32)) adder_1 (.a(PC_q), .b(32'h4), .out(adder_1_out));  // open: cin, cout
  ROM #(.addrWidth(5), .dataWidth(32)) rom_1 (.addr(PC_q[6:2]), .data(RD));  // open: sel
  Adder #(.width(32)) adder_2 (.a(bit_extender_1_out), .b(adder_1_out), .out(adder_2_out));  // open: cin, cout
  and and_1 (and_1_out, Br, Zero);
  Multiplexer #(.width(32)) multiplexer_1 (
    .in0(adder_1_out), .in1(adder_2_out), .out(multiplexer_1_out), .sel(and_1_out));  // open: en

  // Notes on the sheet:
  //   contents of rom_1 (hex, n*v repeats v):
  //   341c0000 341d0000 34013456 210820 8c010004 ac010004 3c027878 411822 3c051234 34040005 0 ac85ffff
  //   8c83ffff 10650001 1000000d 34670404 10e3000b 0 3c087777 3508ffff 80022 34001100 e65020 34080000
  //   34090001 340a0001 10a4020 1109fffe 1000ffff
endmodule

module GRF (
  input  RFReset,
  input  CLK,
  input  WE,
  input  [4:0] A1,
  input  [4:0] A2,
  input  [4:0] A3,
  input  [31:0] WD,
  output [31:0] RD1,
  output [31:0] RD2
);

  wire [31:0] demultiplexer_1_out0, demultiplexer_1_out1, demultiplexer_1_out2, demultiplexer_1_out3,
       demultiplexer_1_out4, demultiplexer_1_out5, demultiplexer_1_out6, demultiplexer_1_out7,
       demultiplexer_1_out8, demultiplexer_1_out9, demultiplexer_1_out10, demultiplexer_1_out11,
       demultiplexer_1_out12, demultiplexer_1_out13, demultiplexer_1_out14, demultiplexer_1_out15,
       demultiplexer_1_out16, demultiplexer_1_out17, demultiplexer_1_out18, demultiplexer_1_out19,
       demultiplexer_1_out20, demultiplexer_1_out21, demultiplexer_1_out22, demultiplexer_1_out23,
       demultiplexer_1_out24, demultiplexer_1_out25, demultiplexer_1_out26, demultiplexer_1_out27,
       demultiplexer_1_out28, demultiplexer_1_out29, demultiplexer_1_out30, demultiplexer_1_out31, out0,
       out1, out2, out3, out4, out5, out6, out7, out8, out9, out10, out11, out12, out13, out14, out15, out16,
       out17, out18, out19, out20, out21, out22, out23, out24, out25, out26, out27, out28, out29, out30,
       out31;

  Demultiplexer #(.select(5), .width(32), .tristate("true")) demultiplexer_1 (
    .out0(demultiplexer_1_out0), .out1(demultiplexer_1_out1), .out2(demultiplexer_1_out2),
    .out3(demultiplexer_1_out3), .out4(demultiplexer_1_out4), .out5(demultiplexer_1_out5),
    .out6(demultiplexer_1_out6), .out7(demultiplexer_1_out7), .out8(demultiplexer_1_out8),
    .out9(demultiplexer_1_out9), .out10(demultiplexer_1_out10), .out11(demultiplexer_1_out11),
    .out12(demultiplexer_1_out12), .out13(demultiplexer_1_out13), .out14(demultiplexer_1_out14),
    .out15(demultiplexer_1_out15), .out16(demultiplexer_1_out16), .out17(demultiplexer_1_out17),
    .out18(demultiplexer_1_out18), .out19(demultiplexer_1_out19), .out20(demultiplexer_1_out20),
    .out21(demultiplexer_1_out21), .out22(demultiplexer_1_out22), .out23(demultiplexer_1_out23),
    .out24(demultiplexer_1_out24), .out25(demultiplexer_1_out25), .out26(demultiplexer_1_out26),
    .out27(demultiplexer_1_out27), .out28(demultiplexer_1_out28), .out29(demultiplexer_1_out29),
    .out30(demultiplexer_1_out30), .out31(demultiplexer_1_out31), .in(WD), .sel(A3));  // open: en
  REG reg_1 (
    .in0(demultiplexer_1_out0), .in1(demultiplexer_1_out1), .in2(demultiplexer_1_out2),
    .in3(demultiplexer_1_out3), .in4(demultiplexer_1_out4), .in5(demultiplexer_1_out5),
    .in6(demultiplexer_1_out6), .in7(demultiplexer_1_out7), .in8(demultiplexer_1_out8),
    .in9(demultiplexer_1_out9), .in10(demultiplexer_1_out10), .in11(demultiplexer_1_out11),
    .in12(demultiplexer_1_out12), .in13(demultiplexer_1_out13), .in14(demultiplexer_1_out14),
    .in15(demultiplexer_1_out15), .in16(demultiplexer_1_out16), .in17(demultiplexer_1_out17),
    .in18(demultiplexer_1_out18), .in19(demultiplexer_1_out19), .in20(demultiplexer_1_out20),
    .in21(demultiplexer_1_out21), .in22(demultiplexer_1_out22), .in23(demultiplexer_1_out23),
    .in24(demultiplexer_1_out24), .in25(demultiplexer_1_out25), .in26(demultiplexer_1_out26),
    .in27(demultiplexer_1_out27), .in28(demultiplexer_1_out28), .in29(demultiplexer_1_out29),
    .in30(demultiplexer_1_out30), .in31(demultiplexer_1_out31), .clk(CLK), .reset(RFReset), .en(WE),
    .out0(out0), .out1(out1), .out2(out2), .out3(out3), .out4(out4), .out5(out5), .out6(out6), .out7(out7),
    .out8(out8), .out9(out9), .out10(out10), .out11(out11), .out12(out12), .out13(out13), .out14(out14),
    .out15(out15), .out16(out16), .out17(out17), .out18(out18), .out19(out19), .out20(out20), .out21(out21),
    .out22(out22), .out23(out23), .out24(out24), .out25(out25), .out26(out26), .out27(out27), .out28(out28),
    .out29(out29), .out30(out30), .out31(out31));
  Multiplexer #(.select(5), .width(32)) multiplexer_1 (
    .in0(out0), .in1(out1), .in2(out2), .in3(out3), .in4(out4), .in5(out5), .in6(out6), .in7(out7),
    .in8(out8), .in9(out9), .in10(out10), .in11(out11), .in12(out12), .in13(out13), .in14(out14),
    .in15(out15), .in16(out16), .in17(out17), .in18(out18), .in19(out19), .in20(out20), .in21(out21),
    .in22(out22), .in23(out23), .in24(out24), .in25(out25), .in26(out26), .in27(out27), .in28(out28),
    .in29(out29), .in30(out30), .in31(out31), .out(RD1), .sel(A1));  // open: en
  Multiplexer #(.select(5), .width(32)) multiplexer_2 (
    .in0(out0), .in1(out1), .in2(out2), .in3(out3), .in4(out4), .in5(out5), .in6(out6), .in7(out7),
    .in8(out8), .in9(out9), .in10(out10), .in11(out11), .in12(out12), .in13(out13), .in14(out14),
    .in15(out15), .in16(out16), .in17(out17), .in18(out18), .in19(out19), .in20(out20), .in21(out21),
    .in22(out22), .in23(out23), .in24(out24), .in25(out25), .in26(out26), .in27(out27), .in28(out28),
    .in29(out29), .in30(out30), .in31(out31), .out(RD2), .sel(A2));  // open: en
endmodule

module REG (
  input  [31:0] in0,
  input  clk,
  input  reset,
  input  en,
  input  [31:0] in1,
  input  [31:0] in2,
  input  [31:0] in3,
  input  [31:0] in4,
  input  [31:0] in5,
  input  [31:0] in6,
  input  [31:0] in7,
  input  [31:0] in8,
  input  [31:0] in9,
  input  [31:0] in10,
  input  [31:0] in11,
  input  [31:0] in12,
  input  [31:0] in13,
  input  [31:0] in14,
  input  [31:0] in15,
  input  [31:0] in16,
  input  [31:0] in17,
  input  [31:0] in18,
  input  [31:0] in19,
  input  [31:0] in20,
  input  [31:0] in21,
  input  [31:0] in22,
  input  [31:0] in23,
  input  [31:0] in24,
  input  [31:0] in25,
  input  [31:0] in26,
  input  [31:0] in27,
  input  [31:0] in28,
  input  [31:0] in29,
  input  [31:0] in30,
  input  [31:0] in31,
  output [31:0] out0,
  output [31:0] out1,
  output [31:0] out2,
  output [31:0] out3,
  output [31:0] out4,
  output [31:0] out5,
  output [31:0] out6,
  output [31:0] out7,
  output [31:0] out8,
  output [31:0] out9,
  output [31:0] out10,
  output [31:0] out11,
  output [31:0] out12,
  output [31:0] out13,
  output [31:0] out14,
  output [31:0] out15,
  output [31:0] out16,
  output [31:0] out17,
  output [31:0] out18,
  output [31:0] out19,
  output [31:0] out20,
  output [31:0] out21,
  output [31:0] out22,
  output [31:0] out23,
  output [31:0] out24,
  output [31:0] out25,
  output [31:0] out26,
  output [31:0] out27,
  output [31:0] out28,
  output [31:0] out29,
  output [31:0] out30,
  output [31:0] out31
);

  Register #(.width(32)) _00 (.D(in0), .en(1'b0), .Q(out0), .clk(clk), .clr(reset));
  Register #(.width(32)) _08 (.D(in8), .en(en), .Q(out8), .clk(clk), .clr(reset));
  Register #(.width(32)) _16 (.D(in16), .en(en), .Q(out16), .clk(clk), .clr(reset));
  Register #(.width(32)) _24 (.D(in24), .en(en), .Q(out24), .clk(clk), .clr(reset));
  Register #(.width(32)) _01 (.D(in1), .en(en), .Q(out1), .clk(clk), .clr(reset));
  Register #(.width(32)) _09 (.D(in9), .en(en), .Q(out9), .clk(clk), .clr(reset));
  Register #(.width(32)) _17 (.D(in17), .en(en), .Q(out17), .clk(clk), .clr(reset));
  Register #(.width(32)) _25 (.D(in25), .en(en), .Q(out25), .clk(clk), .clr(reset));
  Register #(.width(32)) _02 (.D(in2), .en(en), .Q(out2), .clk(clk), .clr(reset));
  Register #(.width(32)) _10 (.D(in10), .en(en), .Q(out10), .clk(clk), .clr(reset));
  Register #(.width(32)) _18 (.D(in18), .en(en), .Q(out18), .clk(clk), .clr(reset));
  Register #(.width(32)) _26 (.D(in26), .en(en), .Q(out26), .clk(clk), .clr(reset));
  Register #(.width(32)) _03 (.D(in3), .en(en), .Q(out3), .clk(clk), .clr(reset));
  Register #(.width(32)) _11 (.D(in11), .en(en), .Q(out11), .clk(clk), .clr(reset));
  Register #(.width(32)) _19 (.D(in19), .en(en), .Q(out19), .clk(clk), .clr(reset));
  Register #(.width(32)) _27 (.D(in27), .en(en), .Q(out27), .clk(clk), .clr(reset));
  Register #(.width(32)) _04 (.D(in4), .en(en), .Q(out4), .clk(clk), .clr(reset));
  Register #(.width(32)) _12 (.D(in12), .en(en), .Q(out12), .clk(clk), .clr(reset));
  Register #(.width(32)) _20 (.D(in20), .en(en), .Q(out20), .clk(clk), .clr(reset));
  Register #(.width(32)) _28 (.D(in28), .en(en), .Q(out28), .clk(clk), .clr(reset));
  Register #(.width(32)) _05 (.D(in5), .en(en), .Q(out5), .clk(clk), .clr(reset));
  Register #(.width(32)) _13 (.D(in13), .en(en), .Q(out13), .clk(clk), .clr(reset));
  Register #(.width(32)) _21 (.D(in21), .en(en), .Q(out21), .clk(clk), .clr(reset));
  Register #(.width(32)) _29 (.D(in29), .en(en), .Q(out29), .clk(clk), .clr(reset));
  Register #(.width(32)) _06 (.D(in6), .en(en), .Q(out6), .clk(clk), .clr(reset));
  Register #(.width(32)) _14 (.D(in14), .en(en), .Q(out14), .clk(clk), .clr(reset));
  Register #(.width(32)) _22 (.D(in22), .en(en), .Q(out22), .clk(clk), .clr(reset));
  Register #(.width(32)) _30 (.D(in30), .en(en), .Q(out30), .clk(clk), .clr(reset));
  Register #(.width(32)) _07 (.D(in7), .en(en), .Q(out7), .clk(clk), .clr(reset));
  Register #(.width(32)) _15 (.D(in15), .en(en), .Q(out15), .clk(clk), .clr(reset));
  Register #(.width(32)) _23 (.D(in23), .en(en), .Q(out23), .clk(clk), .clr(reset));
  Register #(.width(32)) _31 (.D(in31), .en(en), .Q(out31), .clk(clk), .clr(reset));

  // Other names for the same wires on the sheet: res = reset
endmodule

module ALU (
  input  [2:0] ALUOp,
  input  [31:0] SA,
  input  [31:0] SB,
  output out_4,
  output [31:0] ALUResult
);

  wire [31:0] adder_1_out, or_1_out, subtractor_1_out;

  Adder #(.width(32)) adder_1 (.a(SA), .b(SB), .out(adder_1_out));  // open: cin, cout
  assign or_1_out = SA | SB;  // OR_Gate or_1, 32 bits wide
  Comparator #(.width(32), .mode("unsigned")) comparator_1 (.a(SA), .b(SB), .eq(out_4));  // open: gt, lt
  Subtractor #(.width(32)) subtractor_1 (.a(SA), .b(SB), .out(subtractor_1_out));  // open: bin, bout
  Multiplexer #(.select(3), .width(32)) multiplexer_1 (
    .in0(adder_1_out), .in1(subtractor_1_out), .in2(or_1_out), .in3(adder_1_out), .in4(adder_1_out),
    .in5(SB), .in6({32{1'b0}}), .in7({32{1'b0}}), .out(ALUResult), .sel(ALUOp));  // open: en

  // Other names for the same wires on the sheet: Zero = out_4
endmodule

module DM (
  input  CLK,
  input  Wr,
  input  DMReset,
  input  [31:0] A,
  input  [31:0] WD,
  output [31:0] RD
);

  wire not_1_out;

  RAM #(.addrWidth(5), .dataWidth(32), .bus("separate")) ram_1 (
    .addr(A[6:2]), .din(WD), .data(RD), .str(Wr), .clk(CLK), .ld(not_1_out), .clr(DMReset));  // open: sel
  not not_1 (not_1_out, Wr);

  // Other names for the same wires on the sheet: A_t[4:0] = A[6:2]
endmodule

module EXT (
  input  [1:0] EXTOp,
  input  [15:0] imm,
  output [31:0] EXTOut
);

  wire [31:0] bit_extender_1_out, bit_extender_2_out;

  assign bit_extender_1_out = {{16{1'b0}}, imm};  // Bit_Extender bit_extender_1
  assign bit_extender_2_out = {{16{imm[15]}}, imm};  // Bit_Extender bit_extender_2
  Multiplexer #(.select(2), .width(32)) multiplexer_1 (
    .in0(bit_extender_1_out), .in1(bit_extender_2_out), .in2({imm, {16{1'b0}}}), .out(EXTOut), .sel(EXTOp));  // open: in3, en
endmodule

module CTRL (
  input  [5:0] funct,
  input  [5:0] opcode,
  output Br,
  output WRSel,
  output WDSel,
  output RFWE,
  output BSel,
  output DMWR,
  output [1:0] EXTOp,
  output [2:0] ALUOp
);

  wire add_out, beq_out, lui_out, lw_out, nop_out, not_1_out, not_2_out, not_3_out, not_4_out, not_5_out,
       not_6_out, not_7_out, not_8_out, not_9_out, not_10_out, not_11_out, not_12_out, ori_out, sub_out,
       sw_out;

  not not_1 (not_1_out, funct[5]);
  not not_2 (not_2_out, funct[4]);
  not not_3 (not_3_out, funct[3]);
  not not_4 (not_4_out, funct[2]);
  not not_5 (not_5_out, funct[1]);
  not not_6 (not_6_out, funct[0]);
  not not_7 (not_7_out, opcode[5]);
  not not_8 (not_8_out, opcode[4]);
  not not_9 (not_9_out, opcode[3]);
  not not_10 (not_10_out, opcode[2]);
  not not_11 (not_11_out, opcode[1]);
  not not_12 (not_12_out, opcode[0]);
  and add (add_out, not_7_out, not_8_out, not_9_out, not_10_out, not_11_out, not_12_out, funct[5], not_2_out, not_3_out, not_4_out, not_5_out, not_6_out);
  and sub (sub_out, not_7_out, not_8_out, not_9_out, not_10_out, not_11_out, not_12_out, funct[5], not_2_out, not_3_out, not_4_out, funct[1], not_6_out);
  and ori (ori_out, not_7_out, not_8_out, opcode[3], opcode[2], not_11_out, opcode[0]);
  and lw (lw_out, opcode[5], not_8_out, not_9_out, not_10_out, opcode[1], opcode[0]);
  and sw (sw_out, opcode[5], not_8_out, opcode[3], not_10_out, opcode[1], opcode[0]);
  and lui (lui_out, not_7_out, not_8_out, opcode[3], opcode[2], opcode[1], opcode[0]);
  and beq (beq_out, not_7_out, not_8_out, not_9_out, opcode[2], not_11_out, not_12_out);
  and nop (nop_out, not_1_out, not_2_out, not_3_out, not_4_out, not_5_out, not_6_out, not_7_out, not_8_out, not_9_out, not_10_out, not_11_out, not_12_out);
  buf u_Br (Br, beq_out);  // OR_Gate
  or u_WRSel (WRSel, add_out, sub_out);
  buf u_WDSel (WDSel, lw_out);  // OR_Gate
  buf EXTOp1 (EXTOp[1], lui_out);  // OR_Gate
  or EXTOp0 (EXTOp[0], sw_out, lw_out);
  or u_RFWE (RFWE, add_out, sub_out, ori_out, lui_out, lw_out);
  or u_BSel (BSel, ori_out, lw_out, sw_out, lui_out);
  or ALUOp2 (ALUOp[2], lui_out, sw_out);
  or ALUOp1 (ALUOp[1], lw_out, ori_out);
  or ALUOp0 (ALUOp[0], sub_out, lui_out, lw_out);
  buf u_DMWR (DMWR, sw_out);  // OR_Gate
endmodule
