// Logisim project 2^n mod 5.circ as structural Verilog: 3 circuits, main circuit mod5
module mod5 (
  input  in_1,
  output out_2,
  output out_3,
  output out_4,
  output out_5,
  output out_6
);

  wire clock_1_out;
  wire [1:0] register_1_q, transform_1_c0o;

  transform transform_1 (
    .c1(register_1_q[1]), .c0(register_1_q[0]), .b(in_1), .c1o(transform_1_c0o[1]), .c0o(transform_1_c0o[0]));
  Clock clock_1 (.out(clock_1_out));
  Register #(.width(2)) register_1 (.D(transform_1_c0o), .Q(register_1_q), .clk(clock_1_out));  // open: en, clr
  out out_1 (
    .c1(register_1_q[1]), .c0(register_1_q[0]), .b(in_1), .s0(out_2), .s1(out_3), .s2(out_4), .s3(out_5),
    .s4(out_6));
endmodule

module transform (
  input  c1,
  input  c0,
  input  b,
  output c1o,
  output c0o
);

  wire and_1_out, and_2_out, and_3_out, and_4_out, and_5_out, and_6_out, not_1_out, not_2_out, not_3_out,
       not_4_out, not_5_out, not_6_out, not_7_out, not_8_out;

  not not_1 (not_1_out, c1);
  not not_2 (not_2_out, c0);
  not not_3 (not_3_out, c1);
  not not_4 (not_4_out, c0);
  not not_5 (not_5_out, c1);
  not not_6 (not_6_out, b);
  not not_7 (not_7_out, c0);
  not not_8 (not_8_out, b);
  and and_1 (and_1_out, not_1_out, c0);
  and and_2 (and_2_out, c1, not_2_out);
  and and_3 (and_3_out, not_3_out, not_4_out, b);
  and and_4 (and_4_out, not_5_out, c0, not_6_out);
  and and_5 (and_5_out, c1, not_7_out, not_8_out);
  and and_6 (and_6_out, c1, c0, b);
  or or_1 (c1o, and_1_out, and_2_out);
  or or_2 (c0o, and_3_out, and_4_out, and_5_out, and_6_out);
endmodule

module out (
  input  c1,
  input  c0,
  input  b,
  output s0,
  output s1,
  output s2,
  output s3,
  output s4
);

  wire and_1_out, and_2_out, and_3_out, and_4_out, and_5_out, and_6_out, and_7_out, and_8_out, not_1_out,
       not_2_out, not_3_out, not_4_out, not_5_out, not_6_out, not_7_out, not_8_out, not_9_out, not_10_out,
       not_11_out, not_12_out;

  not not_1 (not_1_out, c1);
  not not_2 (not_2_out, c0);
  not not_3 (not_3_out, b);
  not not_4 (not_4_out, b);
  not not_5 (not_5_out, c1);
  not not_6 (not_6_out, c0);
  not not_7 (not_7_out, c1);
  not not_8 (not_8_out, c0);
  not not_9 (not_9_out, c1);
  not not_10 (not_10_out, b);
  not not_11 (not_11_out, c0);
  not not_12 (not_12_out, b);
  and and_1 (and_1_out, not_1_out, not_2_out, not_3_out);
  and and_2 (and_2_out, c1, c0, not_4_out);
  and and_3 (and_3_out, not_5_out, not_6_out, b);
  and and_4 (and_4_out, c1, c0, b);
  and and_5 (and_5_out, not_7_out, c0, b);
  and and_6 (and_6_out, c1, not_8_out, b);
  and and_7 (and_7_out, not_9_out, c0, not_10_out);
  and and_8 (and_8_out, c1, not_11_out, not_12_out);
  or or_1 (s1, and_1_out, and_2_out);
  or or_2 (s2, and_3_out, and_4_out);
  or or_3 (s3, and_5_out, and_6_out);
  or or_4 (s4, and_7_out, and_8_out);

  assign s0 = 1'b0;
endmodule
