// Logisim project fibonacci _challenge.circ as structural Verilog: 8 circuits, main circuit main
module main (
  input  [31:0] in_1,
  output [31:0] out_2
);

  wire count_freeze, count_lsb;

  count count (.in_1(in_1), .lsb(count_lsb), .freeze(count_freeze));
  calculate calculate (.lsb(count_lsb), .freeze(count_freeze), .out_3(out_2));
endmodule

module calculate (
  input  lsb,
  input  freeze,
  output [31:0] out_3
);

  wire clk, ena, select;
  wire [31:0] a11, a12, a21, a22, identitymatrix_1_out_1, identitymatrix_1_out_2, identitymatrix_1_out_3,
       identitymatrix_1_out_4, identitymatrix_2_out_1, identitymatrix_2_out_2, identitymatrix_2_out_3,
       identitymatrix_2_out_4, matrixinitialize_1_out_1, matrixinitialize_1_out_2, matrixinitialize_1_out_3,
       matrixinitialize_1_out_4, matrixmultiply_1_c11, matrixmultiply_1_c12, matrixmultiply_1_c21,
       matrixmultiply_1_c22, matrixmultiply_2_c11, matrixmultiply_2_c12, matrixmultiply_2_c21,
       matrixmultiply_2_c22, matrixselect_1_out_10, matrixselect_1_out_11, matrixselect_1_out_12,
       matrixselect_1_out_13, matrixselect_2_out_10, matrixselect_2_out_11, matrixselect_2_out_12,
       matrixselect_2_out_13, matrixselect_3_out_10, matrixselect_3_out_11, matrixselect_3_out_12,
       matrixselect_3_out_13, s11, s12, s21, s22;

  Counter #(.width(1), .max('h1), .ongoal("stay")) counter_1 (
    .Q(select), .clk(clk));  // open: load, D, count, carry, clr
  Clock clock (.out(clk));
  identityMatrix identitymatrix_1 (
    .out_1(identitymatrix_1_out_1), .out_2(identitymatrix_1_out_2), .out_3(identitymatrix_1_out_3),
    .out_4(identitymatrix_1_out_4));
  matrixInitialize matrixinitialize_1 (
    .out_1(matrixinitialize_1_out_1), .out_2(matrixinitialize_1_out_2), .out_3(matrixinitialize_1_out_3),
    .out_4(matrixinitialize_1_out_4));
  matrixMultiply matrixmultiply_1 (
    .a11(a11), .a12(a12), .a21(a21), .a22(a22), .b11(a11), .b12(a12), .b21(a21), .b22(a22),
    .c11(matrixmultiply_1_c11), .c12(matrixmultiply_1_c12), .c21(matrixmultiply_1_c21),
    .c22(matrixmultiply_1_c22));
  matrixSelect matrixselect_1 (
    .out_10(matrixselect_1_out_10), .out_11(matrixselect_1_out_11), .out_12(matrixselect_1_out_12),
    .out_13(matrixselect_1_out_13), .in_9(lsb), .a11(identitymatrix_1_out_1), .a12(identitymatrix_1_out_2),
    .a21(identitymatrix_1_out_3), .a22(identitymatrix_1_out_4), .b11(a11), .b12(a12), .b21(a21), .b22(a22));
  matrixSelect matrixselect_2 (
    .out_10(matrixselect_2_out_10), .out_11(matrixselect_2_out_11), .out_12(matrixselect_2_out_12),
    .out_13(matrixselect_2_out_13), .in_9(select), .a11(matrixinitialize_1_out_1),
    .a12(matrixinitialize_1_out_2), .a21(matrixinitialize_1_out_3), .a22(matrixinitialize_1_out_4),
    .b11(matrixmultiply_1_c11), .b12(matrixmultiply_1_c12), .b21(matrixmultiply_1_c21),
    .b22(matrixmultiply_1_c22));
  not not_1 (ena, freeze);
  identityMatrix identitymatrix_2 (
    .out_1(identitymatrix_2_out_1), .out_2(identitymatrix_2_out_2), .out_3(identitymatrix_2_out_3),
    .out_4(identitymatrix_2_out_4));
  matrixMultiply matrixmultiply_2 (
    .a11(s11), .a12(s12), .a21(s21), .a22(s22), .b11(matrixselect_1_out_10), .b12(matrixselect_1_out_11),
    .b21(matrixselect_1_out_12), .b22(matrixselect_1_out_13), .c11(matrixmultiply_2_c11),
    .c12(matrixmultiply_2_c12), .c21(matrixmultiply_2_c21), .c22(matrixmultiply_2_c22));
  matrixRegister A (
    .a21_in(matrixselect_2_out_10), .a12_in(matrixselect_2_out_11), .a21_in_2(matrixselect_2_out_12),
    .a22_in(matrixselect_2_out_13), .in_5(ena), .in_6(clk), .a11_out(a11), .a12_out(a12), .a21_out(a21),
    .a22_out(a22));
  matrixRegister S (
    .a21_in(matrixselect_3_out_10), .a12_in(matrixselect_3_out_11), .a21_in_2(matrixselect_3_out_12),
    .a22_in(matrixselect_3_out_13), .in_5(ena), .in_6(clk), .a11_out(s11), .a12_out(s12), .a21_out(s21),
    .a22_out(s22));
  matrixSelect matrixselect_3 (
    .out_10(matrixselect_3_out_10), .out_11(matrixselect_3_out_11), .out_12(matrixselect_3_out_12),
    .out_13(matrixselect_3_out_13), .in_9(select), .a11(identitymatrix_2_out_1),
    .a12(identitymatrix_2_out_2), .a21(identitymatrix_2_out_3), .a22(identitymatrix_2_out_4),
    .b11(matrixmultiply_2_c11), .b12(matrixmultiply_2_c12), .b21(matrixmultiply_2_c21),
    .b22(matrixmultiply_2_c22));
  Multiplexer #(.width(32)) multiplexer_1 (.in0({32{1'b0}}), .in1(s12), .out(out_3), .sel(freeze));  // open: en
endmodule

module count (
  input  [31:0] in_1,
  output lsb,
  output freeze
);

  wire clk, comparator_1_eq, select;
  wire [31:0] multiplexer_1_out, n, shifter_1_out;

  Counter #(.width(1), .max('h1), .ongoal("stay")) counter_1 (
    .Q(select), .clk(clk));  // open: load, D, count, carry, clr
  Clock clock_1 (.out(clk));
  Shifter #(.width(32), .shift("lr")) shifter_1 (.in(n), .\dist (5'b00001), .out(shifter_1_out));
  Bit_Extender #(.in_width(32), .out_width(1)) bit_extender_1 (.in(n), .out(lsb));
  Multiplexer #(.width(32)) multiplexer_1 (
    .in0(in_1), .in1(shifter_1_out), .out(multiplexer_1_out), .sel(select));  // open: en
  Comparator #(.width(32), .mode("unsigned")) comparator_1 (
    .a(n), .b({32{1'b0}}), .eq(comparator_1_eq));  // open: gt, lt
  Register #(.width(32)) register_1 (.D(multiplexer_1_out), .Q(n), .clk(clk));  // open: en, clr
  Multiplexer multiplexer_2 (.in0(1'b0), .in1(comparator_1_eq), .out(freeze), .sel(select));  // open: en

  // Other names for the same wires on the sheet: in[31:0] = in_1
endmodule

module matrixRegister (
  input  [31:0] a21_in,
  input  [31:0] a12_in,
  input  [31:0] a21_in_2,
  input  [31:0] a22_in,
  input  in_5,
  input  in_6,
  output [31:0] a11_out,
  output [31:0] a12_out,
  output [31:0] a21_out,
  output [31:0] a22_out
);

  Register #(.width(32)) a11 (.D(a21_in), .en(in_5), .Q(a11_out), .clk(in_6));  // open: clr
  Register #(.width(32)) a11_2 (.D(a12_in), .en(in_5), .Q(a12_out), .clk(in_6));  // open: clr
  Register #(.width(32)) a21 (.D(a21_in_2), .en(in_5), .Q(a21_out), .clk(in_6));  // open: clr
  Register #(.width(32)) a22 (.D(a22_in), .en(in_5), .Q(a22_out), .clk(in_6));  // open: clr

  // Other names for the same wires on the sheet: a11_in[31:0] = a21_in; a21_in_t[31:0] = a21_in_2; clk = in_6;
  //   ena = in_5
endmodule

// Multiply
module matrixMultiply (
  input  [31:0] a11,
  input  [31:0] a12,
  input  [31:0] a21,
  input  [31:0] a22,
  input  [31:0] b11,
  input  [31:0] b12,
  input  [31:0] b21,
  input  [31:0] b22,
  output [31:0] c11,
  output [31:0] c12,
  output [31:0] c21,
  output [31:0] c22
);

  wire [31:0] multiplier_1_out, multiplier_2_out, multiplier_3_out, multiplier_4_out, multiplier_5_out,
       multiplier_6_out, multiplier_7_out, multiplier_8_out;

  Multiplier #(.width(32)) multiplier_1 (.a(a11), .b(b11), .out(multiplier_1_out));  // open: cin, cout
  Multiplier #(.width(32)) multiplier_2 (.a(a12), .b(b21), .out(multiplier_2_out));  // open: cin, cout
  Multiplier #(.width(32)) multiplier_3 (.a(a11), .b(b12), .out(multiplier_3_out));  // open: cin, cout
  Multiplier #(.width(32)) multiplier_4 (.a(a12), .b(b22), .out(multiplier_4_out));  // open: cin, cout
  Multiplier #(.width(32)) multiplier_5 (.a(a21), .b(b11), .out(multiplier_5_out));  // open: cin, cout
  Multiplier #(.width(32)) multiplier_6 (.a(a22), .b(b21), .out(multiplier_6_out));  // open: cin, cout
  Multiplier #(.width(32)) multiplier_7 (.a(a21), .b(b12), .out(multiplier_7_out));  // open: cin, cout
  Multiplier #(.width(32)) multiplier_8 (.a(a22), .b(b22), .out(multiplier_8_out));  // open: cin, cout
  Adder #(.width(32)) adder_1 (.a(multiplier_1_out), .b(multiplier_2_out), .out(c11));  // open: cin, cout
  Adder #(.width(32)) adder_2 (.a(multiplier_3_out), .b(multiplier_4_out), .out(c12));  // open: cin, cout
  Adder #(.width(32)) adder_3 (.a(multiplier_5_out), .b(multiplier_6_out), .out(c21));  // open: cin, cout
  Adder #(.width(32)) adder_4 (.a(multiplier_7_out), .b(multiplier_8_out), .out(c22));  // open: cin, cout
endmodule

// Select
module matrixSelect (
  input  [31:0] a11,
  input  [31:0] a12,
  input  [31:0] a21,
  input  [31:0] a22,
  input  [31:0] b11,
  input  [31:0] b12,
  input  [31:0] b21,
  input  [31:0] b22,
  input  in_9,
  output [31:0] out_10,
  output [31:0] out_11,
  output [31:0] out_12,
  output [31:0] out_13
);

  Multiplexer #(.width(32)) multiplexer_1 (.in0(a11), .in1(b11), .out(out_10), .sel(in_9));  // open: en
  Multiplexer #(.width(32)) multiplexer_2 (.in0(a12), .in1(b12), .out(out_11), .sel(in_9));  // open: en
  Multiplexer #(.width(32)) multiplexer_3 (.in0(a21), .in1(b21), .out(out_12), .sel(in_9));  // open: en
  Multiplexer #(.width(32)) multiplexer_4 (.in0(a22), .in1(b22), .out(out_13), .sel(in_9));  // open: en

  // Other names for the same wires on the sheet: c11[31:0] = out_10; c12[31:0] = out_11; c21[31:0] = out_12;
  //   c22[31:0] = out_13; select = in_9
endmodule

// Init
module matrixInitialize (
  output [31:0] out_1,
  output [31:0] out_2,
  output [31:0] out_3,
  output [31:0] out_4
);


  assign out_1 = 32'h1;
  assign out_2 = 32'h1;
  assign out_3 = 32'h1;
  assign out_4 = {32{1'b0}};
endmodule

// id
module identityMatrix (
  output [31:0] out_1,
  output [31:0] out_2,
  output [31:0] out_3,
  output [31:0] out_4
);


  assign out_1 = 32'h1;
  assign out_2 = {32{1'b0}};
  assign out_3 = {32{1'b0}};
  assign out_4 = 32'h1;
endmodule
