// Logisim project fibonacci.circ as structural Verilog: 3 circuits, main circuit main
module main (
  input  [2:0] in_1,
  output [3:0] out_2
);

  wire count_out_2;
  wire [3:0] calculate_out_2;

  count count (.in_1(in_1), .out_2(count_out_2));
  calculate calculate (.freeze(count_out_2), .out_2(calculate_out_2));
  Multiplexer #(.width(4)) multiplexer_1 (
    .in0(4'b0001), .in1(calculate_out_2), .out(out_2), .sel(count_out_2));  // open: en
endmodule

module calculate (
  input  freeze,
  output [3:0] out_2
);

  wire clock, counter_1_q, freeze_t;
  wire [3:0] adder_1_out, multiplexer_1_out, prev;

  Clock u_clock (.out(clock));
  not not_1 (freeze_t, freeze);
  Counter #(.width(1), .max('h1), .ongoal("stay")) counter_1 (
    .Q(counter_1_q), .clk(clock));  // open: load, D, count, carry, clr
  Adder #(.width(4)) adder_1 (.a(prev), .b(out_2), .out(adder_1_out));  // open: cin, cout
  Multiplexer #(.width(4)) multiplexer_1 (
    .in0(4'b0001), .in1(out_2), .out(multiplexer_1_out), .sel(counter_1_q));  // open: en
  Register #(.width(4)) u_prev (.D(multiplexer_1_out), .en(freeze_t), .Q(prev), .clk(clock));  // open: clr
  Register #(.width(4)) now (.D(adder_1_out), .en(freeze_t), .Q(out_2), .clk(clock));  // open: clr

  // Other names for the same wires on the sheet: now[3:0] = out_2
endmodule

module count (
  input  [2:0] in_1,
  output out_2
);

  wire clock_1_out;
  wire [3:0] bit_extender_1_out, counter_1_q;

  assign bit_extender_1_out = {{1{1'b0}}, in_1};  // Bit_Extender bit_extender_1
  Counter #(.width(4), .max('hf), .ongoal("stay")) counter_1 (
    .Q(counter_1_q), .clk(clock_1_out));  // open: load, D, count, carry, clr
  Clock clock_1 (.out(clock_1_out));
  Comparator #(.width(4), .mode("unsigned")) comparator_1 (
    .a(bit_extender_1_out), .b(counter_1_q), .lt(out_2));  // open: gt, eq
endmodule
