// Logisim project sort.circ as structural Verilog: 3 circuits, main circuit 1bit_swap
module _1bit_swap (
  input  I1,
  input  I2,
  input  S,
  output O1,
  output O2
);

  wire and_1_out, and_2_out, and_3_out, and_4_out, and_5_out, and_6_out;

  and and_1 (and_1_out, I1, I2, S);
  and and_2 (and_2_out, S, ~I1, I2);  // AND_Gate
  and and_3 (and_3_out, ~S, I1, I2);  // AND_Gate
  and and_4 (and_4_out, ~S, ~I2, I1);  // AND_Gate
  and and_5 (and_5_out, S, I1, ~I2);  // AND_Gate
  and and_6 (and_6_out, ~S, ~I1, I2);  // AND_Gate
  or or_1 (O1, and_1_out, and_2_out, and_3_out, and_4_out);
  or or_2 (O2, and_1_out, and_3_out, and_5_out, and_6_out);
endmodule

module _4bit_swap (
  input  [3:0] I1,
  input  [3:0] I2,
  input  S,
  output [3:0] O1,
  output [3:0] O2
);

  _1bit_swap u_1bit_swap_1 (.I1(I1[0]), .O1(O1[0]), .I2(I2[0]), .O2(O2[0]), .S(S));
  _1bit_swap u_1bit_swap_2 (.I1(I1[1]), .O1(O1[1]), .I2(I2[1]), .O2(O2[1]), .S(S));
  _1bit_swap u_1bit_swap_3 (.I1(I1[2]), .O1(O1[2]), .I2(I2[2]), .O2(O2[2]), .S(S));
  _1bit_swap u_1bit_swap_4 (.I1(I1[3]), .O1(O1[3]), .I2(I2[3]), .O2(O2[3]), .S(S));
endmodule

module _4bit_sort (
  input  [3:0] in_1,
  input  [3:0] in_2,
  input  [3:0] in_3,
  input  [3:0] in_4,
  output [3:0] out_5,
  output [3:0] out_6,
  output [3:0] out_7,
  output [3:0] out_8
);

  wire comparator_1_gt, comparator_2_gt, comparator_3_gt, comparator_4_gt, comparator_5_gt, comparator_6_gt;
  wire [3:0] n4bit_swap_1_o1, n4bit_swap_1_o2, n4bit_swap_2_o1, n4bit_swap_2_o2, n4bit_swap_3_o1,
       n4bit_swap_3_o2, n4bit_swap_4_o1, n4bit_swap_5_o1;

  _4bit_swap u_4bit_swap_1 (.I1(in_1), .I2(in_2), .S(comparator_1_gt), .O1(n4bit_swap_1_o1), .O2(n4bit_swap_1_o2));
  Comparator #(.width(4), .mode("unsigned")) comparator_1 (.a(in_1), .b(in_2), .gt(comparator_1_gt));  // open: eq, lt
  _4bit_swap u_4bit_swap_2 (
    .I1(n4bit_swap_1_o2), .I2(in_3), .S(comparator_2_gt), .O1(n4bit_swap_2_o1), .O2(n4bit_swap_2_o2));
  Comparator #(.width(4), .mode("unsigned")) comparator_2 (
    .a(n4bit_swap_1_o2), .b(in_3), .gt(comparator_2_gt));  // open: eq, lt
  Comparator #(.width(4), .mode("unsigned")) comparator_3 (
    .a(n4bit_swap_1_o1), .b(n4bit_swap_2_o1), .gt(comparator_3_gt));  // open: eq, lt
  Comparator #(.width(4), .mode("unsigned")) comparator_4 (
    .a(n4bit_swap_2_o2), .b(in_4), .gt(comparator_4_gt));  // open: eq, lt
  _4bit_swap u_4bit_swap_3 (
    .I1(n4bit_swap_1_o1), .I2(n4bit_swap_2_o1), .S(comparator_3_gt), .O1(n4bit_swap_3_o1),
    .O2(n4bit_swap_3_o2));
  Comparator #(.width(4), .mode("unsigned")) comparator_5 (
    .a(n4bit_swap_3_o2), .b(n4bit_swap_4_o1), .gt(comparator_5_gt));  // open: eq, lt
  _4bit_swap u_4bit_swap_4 (.I1(n4bit_swap_2_o2), .I2(in_4), .S(comparator_4_gt), .O1(n4bit_swap_4_o1), .O2(out_8));
  _4bit_swap u_4bit_swap_5 (
    .I1(n4bit_swap_3_o2), .I2(n4bit_swap_4_o1), .S(comparator_5_gt), .O1(n4bit_swap_5_o1), .O2(out_7));
  Comparator #(.width(4), .mode("unsigned")) comparator_6 (
    .a(n4bit_swap_3_o1), .b(n4bit_swap_5_o1), .gt(comparator_6_gt));  // open: eq, lt
  _4bit_swap u_4bit_swap_6 (.I1(n4bit_swap_3_o1), .I2(n4bit_swap_5_o1), .S(comparator_6_gt), .O1(out_5), .O2(out_6));
endmodule
