// Logisim project swap.circ as structural Verilog: 1 circuit, main circuit swap
module swap (
  input  I1,
  input  I2,
  input  S,
  output O1,
  output O2
);

  wire and_1_out, and_2_out, and_3_out, and_4_out, and_5_out, and_6_out;

  and and_1 (and_1_out, I1, I2, S);
  and and_2 (and_2_out, S, ~I1, I2);  // AND_Gate
  and and_3 (and_3_out, ~S, I1, I2);  // AND_Gate
  and and_4 (and_4_out, ~S, ~I2, I1);  // AND_Gate
  and and_5 (and_5_out, S, I1, ~I2);  // AND_Gate
  and and_6 (and_6_out, ~S, ~I1, I2);  // AND_Gate
  or or_1 (O1, and_1_out, and_2_out, and_3_out, and_4_out);
  or or_2 (O2, and_1_out, and_3_out, and_5_out, and_6_out);
endmodule
